// Logisim project BSCS23107_CA_Project.circ as structural Verilog: 23 circuits, main circuit main
module main (
  input  in_1,
  output [3:0] out_2,
  output [15:0] out_3,
  output [15:0] out_4,
  output [15:0] out_5,
  output [15:0] out_6,
  output [15:0] out_7,
  output [15:0] out_8,
  output [3:0] out_9
);

  wire ac_controller_1_ac_clr, ac_controller_1_ac_inc, ac_controller_1_ac_ld, ar_controller_1_ar_clr,
       ar_controller_1_ar_inc, ar_controller_1_ar_ld, bus_controlle1r_1_x1, bus_controlle1r_1_x2,
       bus_controlle1r_1_x3, bus_controlle1r_1_x4, bus_controlle1r_1_x5, bus_controlle1r_1_x6,
       bus_controlle1r_1_x7, bus_encoder_8x3_1_s0, bus_encoder_8x3_1_s1, bus_encoder_8x3_1_s2, CLK,
       dr_controller_1_dr_inc, dr_controller_1_dr_ld, E, E_ALU, E_clr, E_set, FGI, FGI_clr, FGO, FGOclr, I,
       I_set, IEN, IEN_clr, IEN_set, ir_controller_1_ir_ld, MCLK, not_1_out, outr_controller_1_outr_ld,
       pc_controller_1_pc_clr, pc_controller_1_pc_inc, pc_controller_1_pc_ld, R, R_clr, R_set, ram_cu_1_read,
       ram_cu_1_write, S, S_clr, S_set, sc_controller_1_sc_clr_out, scounter_1_cry, tr_controller_1_tr_ld,
       undriven;
  wire [7:0] INPR_IN, INPR_OUT, OUTR_OUT;
  wire [15:0] ALU_OUT, BUS_OUT, TR;

  SC_CONTROLLER sc_controller_1 (.IR(out_8), .Timer(out_2), .R(R), .SC_CLR_Out(sc_controller_1_sc_clr_out));
  RAM_CU ram_cu_1 (.IR(out_8), .Timer(out_2), .R(R), .Read(ram_cu_1_read), .Write(ram_cu_1_write));
  not not_1 (not_1_out, S);
  Clock clock_1 (.out(CLK));
  RAM #(.addrWidth(12), .asyncread("true"), .dataWidth(16)) ram_1 (
    .addr(out_4[11:0]), .we(ram_cu_1_write), .oe(ram_cu_1_read), .clk(CLK), .din(BUS_OUT), .dout(out_3));
  ALU1 alu1_1 (
    .IR(out_8), .Timer(out_2), .Ebit(E), .AC(out_6), .DR(out_7), .INPR(INPR_OUT), .ALU_OP(ALU_OUT),
    .ExtendedBit(E_ALU));
  SCOUNTER scounter_1 (
    .CLR(sc_controller_1_sc_clr_out), .LD(undriven), .STRT(not_1_out), .CLK(CLK), .O(out_2),
    .Cry(scounter_1_cry));  // open: I
  PC_CONTROLLER pc_controller_1 (
    .IR(out_8), .Timer(out_2), .R(R), .DR(out_7), .AC(out_6), .E(E), .FGI(FGI), .FGO(FGO),
    .PC_LD(pc_controller_1_pc_ld), .PC_INC(pc_controller_1_pc_inc), .PC_CLR(pc_controller_1_pc_clr));
  AR_CONTROLLER ar_controller_1 (
    .IR(out_8), .Timer(out_2), .R(R), .AR_LD(ar_controller_1_ar_ld), .AR_INC(ar_controller_1_ar_inc),
    .AR_CLR(ar_controller_1_ar_clr));
  DR_CONTROLLER dr_controller_1 (
    .IR(out_8), .Timer(out_2), .DR_LD(dr_controller_1_dr_ld), .DR_INC(dr_controller_1_dr_inc));
  AC_CONTROLLER ac_controller_1 (
    .IR(out_8), .Timer(out_2), .AC_INC(ac_controller_1_ac_inc), .AC_CLR(ac_controller_1_ac_clr),
    .AC_LD(ac_controller_1_ac_ld));
  IR_CONTROLLER ir_controller_1 (.R(R), .Timer(out_2), .IR_LD(ir_controller_1_ir_ld));
  TR_CONTROLLER tr_controller_1 (.R(R), .Timer(out_2), .TR_LD(tr_controller_1_tr_ld));
  OUTR_CONTROLLER outr_controller_1 (.IR(out_8), .Timer(out_2), .OUTR_LD(outr_controller_1_outr_ld));
  bit12reg AR (
    .LD(ar_controller_1_ar_ld), .INC(ar_controller_1_ar_inc), .CLR(ar_controller_1_ar_clr), .CK(CLK),
    .I1(BUS_OUT), .O1(out_4));
  bit12reg PC (
    .LD(pc_controller_1_pc_ld), .INC(pc_controller_1_pc_inc), .CLR(pc_controller_1_pc_clr), .CK(CLK),
    .I1(BUS_OUT), .O1(out_5));
  bit16reg DR (
    .LD(dr_controller_1_dr_ld), .INC(dr_controller_1_dr_inc), .CK(CLK), .I1(BUS_OUT), .O1(out_7));  // open: CLR
  bit16reg AC (
    .LD(ac_controller_1_ac_ld), .INC(ac_controller_1_ac_inc), .CLR(ac_controller_1_ac_clr), .CK(CLK),
    .I1(ALU_OUT), .O1(out_6));
  INPR1 inpr1_1 (.I1(INPR_IN), .O(INPR_OUT));
  bit16reg IR (.LD(ir_controller_1_ir_ld), .CK(CLK), .I1(BUS_OUT), .O1(out_8));  // open: INC, CLR
  bit16reg u_TR (.LD(tr_controller_1_tr_ld), .CK(CLK), .I1(BUS_OUT), .O1(TR));  // open: INC, CLR
  OUTR1 outr1_1 (.LD(outr_controller_1_outr_ld), .CK(CLK), .I1(BUS_OUT), .O(OUTR_OUT));  // open: CLR
  BUS_CONTROLLE1R bus_controlle1r_1 (
    .IR(out_8), .Timer(out_2), .R(R), .X1(bus_controlle1r_1_x1), .X2(bus_controlle1r_1_x2),
    .X3(bus_controlle1r_1_x3), .X4(bus_controlle1r_1_x4), .X5(bus_controlle1r_1_x5),
    .X6(bus_controlle1r_1_x6), .X7(bus_controlle1r_1_x7));
  BUS_Encoder_8x3 bus_encoder_8x3_1 (
    .X1(bus_controlle1r_1_x1), .X2(bus_controlle1r_1_x2), .X3(bus_controlle1r_1_x3),
    .X4(bus_controlle1r_1_x4), .X5(bus_controlle1r_1_x5), .X6(bus_controlle1r_1_x6),
    .X7(bus_controlle1r_1_x7), .S0(bus_encoder_8x3_1_s0), .S1(bus_encoder_8x3_1_s1), .S2(bus_encoder_8x3_1_s2));
  BUS_BLOCK1 bus_block1_1 (
    .AR(out_4), .PC(out_5), .DR(out_7), .AC(out_6), .IR(out_8), .TR(TR), .MEM(out_3),
    .S2(bus_encoder_8x3_1_s2), .S1(bus_encoder_8x3_1_s1), .S0(bus_encoder_8x3_1_s0), .O(BUS_OUT));
  FF_Controller1 ff_controller1_1 (
    .MCLK(CLK), .STRT(in_1), .IR(out_8), .Timer(out_2), .R(R), .IEN(IEN), .FGI(FGI), .FGO(FGO),
    .E_ALU_OUT(E_ALU), .MCK(MCLK), .I_set(I_set), .S_set(S_set), .S_clr(S_clr), .R_set(R_set), .R_clr(R_clr),
    .IEN_set(IEN_set), .IEN_clr(IEN_clr), .FGI_clr(FGI_clr), .FGO_clr(FGOclr), .E_set(E_set), .E_clr(E_clr));
  J_K_Flip_Flop j_k_ff_1 (.J(I_set), .clk(MCLK), .Q(I));  // open: K, Qn, preset, reset
  J_K_Flip_Flop j_k_ff_2 (.J(S_set), .K(S_clr), .clk(MCLK), .Q(S));  // open: Qn, preset, reset
  J_K_Flip_Flop j_k_ff_3 (.J(R_set), .K(R_clr), .clk(MCLK), .Q(R));  // open: Qn, preset, reset
  J_K_Flip_Flop j_k_ff_4 (.J(IEN_set), .K(IEN_clr), .clk(MCLK), .Q(IEN));  // open: Qn, preset, reset
  J_K_Flip_Flop j_k_ff_5 (.K(FGI_clr), .clk(MCLK), .Q(FGI));  // open: J, Qn, preset, reset
  J_K_Flip_Flop j_k_ff_6 (.K(FGOclr), .clk(MCLK), .Q(FGO));  // open: J, Qn, preset, reset
  J_K_Flip_Flop j_k_ff_7 (.J(E_set), .K(E_clr), .clk(MCLK), .Q(E));  // open: Qn, preset, reset

  assign out_9 = out_2;
  // also tied to GND on the sheet: scounter_1_cry

  // Other names for the same wires on the sheet: AR[15:0] = out_4; AC[15:0] = out_6; DR[15:0] = out_7;
  //   IR[15:0] = out_8; PC[15:0] = out_5; RAM_OUT[15:0] = out_3; SC[3:0] = out_2

  // Notes on the sheet:
  //   Master Clock
endmodule

module bit16reg (
  input  LD,
  input  INC,
  input  CLR,
  input  CK,
  input  [15:0] I1,
  output [15:0] O1
);

  wire and_2_out, not_1_out, SL1;
  wire [15:0] adder_1_out, d1_q, multiplexer_1_out;

  not not_1 (not_1_out, LD);
  Multiplexer #(.width(16)) multiplexer_1 (.in0(O1), .in1(I1), .out(multiplexer_1_out), .sel(LD));
  and and_1 (SL1, not_1_out, INC);
  and and_2 (and_2_out, CLR, CK);
  D_Flip_Flop d1 (.D(multiplexer_1_out[0]), .clk(CK), .Q(d1_q[0]), .reset(and_2_out));  // open: Qn, preset
  D_Flip_Flop d2 (.D(multiplexer_1_out[1]), .clk(CK), .Q(d1_q[1]), .reset(and_2_out));  // open: Qn, preset
  D_Flip_Flop d3 (.D(multiplexer_1_out[2]), .clk(CK), .Q(d1_q[2]), .reset(and_2_out));  // open: Qn, preset
  D_Flip_Flop d4 (.D(multiplexer_1_out[3]), .clk(CK), .Q(d1_q[3]), .reset(and_2_out));  // open: Qn, preset
  D_Flip_Flop d5 (.D(multiplexer_1_out[4]), .clk(CK), .Q(d1_q[4]), .reset(and_2_out));  // open: Qn, preset
  D_Flip_Flop d6 (.D(multiplexer_1_out[5]), .clk(CK), .Q(d1_q[5]), .reset(and_2_out));  // open: Qn, preset
  D_Flip_Flop d7 (.D(multiplexer_1_out[6]), .clk(CK), .Q(d1_q[6]), .reset(and_2_out));  // open: Qn, preset
  D_Flip_Flop d8 (.D(multiplexer_1_out[7]), .clk(CK), .Q(d1_q[7]), .reset(and_2_out));  // open: Qn, preset
  D_Flip_Flop d9 (.D(multiplexer_1_out[8]), .clk(CK), .Q(d1_q[8]), .reset(and_2_out));  // open: Qn, preset
  D_Flip_Flop d10 (.D(multiplexer_1_out[9]), .clk(CK), .Q(d1_q[9]), .reset(and_2_out));  // open: Qn, preset
  D_Flip_Flop d11 (.D(multiplexer_1_out[10]), .clk(CK), .Q(d1_q[10]), .reset(and_2_out));  // open: Qn, preset
  D_Flip_Flop d12 (.D(multiplexer_1_out[11]), .clk(CK), .Q(d1_q[11]), .reset(and_2_out));  // open: Qn, preset
  D_Flip_Flop d13 (.D(multiplexer_1_out[12]), .clk(CK), .Q(d1_q[12]), .reset(and_2_out));  // open: Qn, preset
  D_Flip_Flop d14 (.D(multiplexer_1_out[13]), .clk(CK), .Q(d1_q[13]), .reset(and_2_out));  // open: Qn, preset
  D_Flip_Flop d15 (.D(multiplexer_1_out[14]), .clk(CK), .Q(d1_q[14]), .reset(and_2_out));  // open: Qn, preset
  D_Flip_Flop d16 (.D(multiplexer_1_out[15]), .clk(CK), .Q(d1_q[15]), .reset(and_2_out));  // open: Qn, preset
  Adder #(.width(16)) adder_1 (.a(d1_q), .b({16{1'b0}}), .out(adder_1_out), .cin(1'b1));  // open: cout
  Multiplexer #(.width(16)) multiplexer_2 (.in0(d1_q), .in1(adder_1_out), .out(O1), .sel(INC));

  // Other names for the same wires on the sheet: INC1 = INC; INCo[15:0] = O1; LD1 = LD

  // Notes on the sheet:
  //   on ld =0 and inc=0 , it will do nothing 
  //   on ld = 1 and inc = 0 , it will load
  //   on ld =0 and inc =1 , it will increment
  //   on ld =1 and inc =1 , it will load
  //   selectes load(0) or INC(1) 
  //   adds 1
  //   selectes load(0) or INC(1) 
  //   takes incremented value back to register
endmodule

module bit12reg (
  input  LD,
  input  INC,
  input  CLR,
  input  CK,
  input  [15:0] I1,
  output [15:0] O1
);

  wire and_2_out, not_1_out, SL1;
  wire [11:0] adder_1_out, d1_q, multiplexer_1_out;

  not not_1 (not_1_out, LD);
  Multiplexer #(.width(12)) multiplexer_1 (.in0(O1[11:0]), .in1(I1[11:0]), .out(multiplexer_1_out), .sel(LD));
  and and_1 (SL1, not_1_out, INC);
  and and_2 (and_2_out, CLR, CK);
  D_Flip_Flop d1 (.D(multiplexer_1_out[0]), .clk(CK), .Q(d1_q[0]), .reset(and_2_out));  // open: Qn, preset
  D_Flip_Flop d2 (.D(multiplexer_1_out[1]), .clk(CK), .Q(d1_q[1]), .reset(and_2_out));  // open: Qn, preset
  D_Flip_Flop d3 (.D(multiplexer_1_out[2]), .clk(CK), .Q(d1_q[2]), .reset(and_2_out));  // open: Qn, preset
  D_Flip_Flop d4 (.D(multiplexer_1_out[3]), .clk(CK), .Q(d1_q[3]), .reset(and_2_out));  // open: Qn, preset
  D_Flip_Flop d5 (.D(multiplexer_1_out[4]), .clk(CK), .Q(d1_q[4]), .reset(and_2_out));  // open: Qn, preset
  D_Flip_Flop d6 (.D(multiplexer_1_out[5]), .clk(CK), .Q(d1_q[5]), .reset(and_2_out));  // open: Qn, preset
  D_Flip_Flop d7 (.D(multiplexer_1_out[6]), .clk(CK), .Q(d1_q[6]), .reset(and_2_out));  // open: Qn, preset
  D_Flip_Flop d8 (.D(multiplexer_1_out[7]), .clk(CK), .Q(d1_q[7]), .reset(and_2_out));  // open: Qn, preset
  D_Flip_Flop d9 (.D(multiplexer_1_out[8]), .clk(CK), .Q(d1_q[8]), .reset(and_2_out));  // open: Qn, preset
  D_Flip_Flop d10 (.D(multiplexer_1_out[9]), .clk(CK), .Q(d1_q[9]), .reset(and_2_out));  // open: Qn, preset
  D_Flip_Flop d11 (.D(multiplexer_1_out[10]), .clk(CK), .Q(d1_q[10]), .reset(and_2_out));  // open: Qn, preset
  D_Flip_Flop d12 (.D(multiplexer_1_out[11]), .clk(CK), .Q(d1_q[11]), .reset(and_2_out));  // open: Qn, preset
  Adder #(.width(12)) adder_1 (.a(d1_q), .b({12{1'b0}}), .out(adder_1_out), .cin(1'b1));  // open: cout
  Multiplexer #(.width(12)) multiplexer_2 (.in0(d1_q), .in1(adder_1_out), .out(O1[11:0]), .sel(INC));

  assign O1[15:12] = 4'b0000;

  // Other names for the same wires on the sheet: INC1 = INC; LD1 = LD; INCo[11:0] = O1[11:0]

  // Notes on the sheet:
  //   on ld =0 and inc=0 , it will do nothing 
  //   on ld = 1 and inc = 0 , it will load
  //   on ld =0 and inc =1 , it will increment
  //   on ld =1 and inc =1 , it will load
  //   selectes load(0) or INC(1) 
  //   adds 1
  //   selectes load(0) or INC(1) 
  //   takes incremented value back to register
endmodule

module bit8reg (
  input  LD,
  input  INC,
  input  CLR,
  input  CK,
  input  [7:0] I1,
  output [7:0] O1
);

  wire and_2_out, and_3_out, not_1_out, or_1_out, SL1;
  wire [7:0] d1_q, INCo, multiplexer_1_out;

  not not_1 (not_1_out, LD);
  Multiplexer #(.width(8)) multiplexer_1 (.in0(I1), .in1(INCo), .out(multiplexer_1_out), .sel(SL1));
  and and_1 (SL1, not_1_out, INC);
  or or_1 (or_1_out, LD, INC);
  and and_2 (and_2_out, CLR, CK);
  and and_3 (and_3_out, or_1_out, CK);
  D_Flip_Flop d1 (.D(multiplexer_1_out[0]), .clk(and_3_out), .Q(d1_q[0]), .reset(and_2_out));  // open: Qn, preset
  D_Flip_Flop d2 (.D(multiplexer_1_out[1]), .clk(and_3_out), .Q(d1_q[1]), .reset(and_2_out));  // open: Qn, preset
  D_Flip_Flop d3 (.D(multiplexer_1_out[2]), .clk(and_3_out), .Q(d1_q[2]), .reset(and_2_out));  // open: Qn, preset
  D_Flip_Flop d4 (.D(multiplexer_1_out[3]), .clk(and_3_out), .Q(d1_q[3]), .reset(and_2_out));  // open: Qn, preset
  D_Flip_Flop d5 (.D(multiplexer_1_out[4]), .clk(and_3_out), .Q(d1_q[4]), .reset(and_2_out));  // open: Qn, preset
  D_Flip_Flop d6 (.D(multiplexer_1_out[5]), .clk(and_3_out), .Q(d1_q[5]), .reset(and_2_out));  // open: Qn, preset
  D_Flip_Flop d7 (.D(multiplexer_1_out[6]), .clk(and_3_out), .Q(d1_q[6]), .reset(and_2_out));  // open: Qn, preset
  D_Flip_Flop d8 (.D(multiplexer_1_out[7]), .clk(and_3_out), .Q(d1_q[7]), .reset(and_2_out));  // open: Qn, preset
  Adder adder_1 (.a(d1_q), .b({8{1'b0}}), .out(INCo), .cin(1'b1));  // open: cout
  Multiplexer #(.width(8)) multiplexer_2 (.in0(d1_q), .in1(INCo), .out(O1), .sel(SL1));

  // Other names for the same wires on the sheet: INC1 = INC; LD1 = LD

  // Notes on the sheet:
  //   on ld =0 and inc=0 , it will do nothing 
  //   on ld = 1 and inc = 0 , it will load
  //   on ld =0 and inc =1 , it will increment
  //   on ld =1 and inc =1 , it will load
  //   selectes load(0) or INC(1) 
  //   adds 1
  //   selectes load(0) or INC(1) 
  //   takes incremented value back to register
endmodule

module RAM_BLOCK1 (
  input  [15:0] DATA_IN,
  input  RD,
  input  WR,
  input  CK,
  input  [11:0] Add_IN,
  output [15:0] O
);

  wire decoder_1_out0, decoder_1_out1, decoder_1_out2, decoder_1_out3, decoder_1_out4, decoder_1_out5,
       decoder_1_out6, decoder_1_out7, decoder_1_out8, decoder_1_out9, decoder_1_out10, decoder_1_out11,
       decoder_1_out12, decoder_1_out13, decoder_1_out14, decoder_1_out15, decoder_1_out16, decoder_1_out17,
       decoder_1_out18, decoder_1_out19, decoder_1_out20, decoder_1_out21, decoder_1_out22, decoder_1_out23,
       decoder_1_out24, decoder_1_out25, decoder_1_out26, decoder_1_out27, decoder_1_out28, decoder_1_out29,
       decoder_1_out30, decoder_1_out31;
  wire [15:0] demultiplexer_1_out0, demultiplexer_1_out1, demultiplexer_1_out2, demultiplexer_1_out3,
       demultiplexer_1_out4, demultiplexer_1_out5, demultiplexer_1_out6, demultiplexer_1_out7,
       demultiplexer_1_out8, demultiplexer_1_out9, demultiplexer_1_out10, demultiplexer_1_out11,
       demultiplexer_1_out12, demultiplexer_1_out13, demultiplexer_1_out14, demultiplexer_1_out15,
       demultiplexer_1_out16, demultiplexer_1_out17, demultiplexer_1_out18, demultiplexer_1_out19,
       demultiplexer_1_out20, demultiplexer_1_out21, demultiplexer_1_out22, demultiplexer_1_out23,
       demultiplexer_1_out24, demultiplexer_1_out25, demultiplexer_1_out26, demultiplexer_1_out27,
       demultiplexer_1_out28, demultiplexer_1_out29, demultiplexer_1_out30, demultiplexer_1_out31,
       memreg_1_o1, memreg_2_o1, memreg_3_o1, memreg_4_o1, memreg_5_o1, memreg_6_o1, memreg_7_o1,
       memreg_8_o1, memreg_9_o1, memreg_10_o1, memreg_11_o1, memreg_12_o1, memreg_13_o1, memreg_14_o1,
       memreg_15_o1, memreg_16_o1, memreg_17_o1, memreg_18_o1, memreg_19_o1, memreg_20_o1, memreg_21_o1,
       memreg_22_o1, memreg_23_o1, memreg_24_o1, memreg_25_o1, memreg_26_o1, memreg_27_o1, memreg_28_o1,
       memreg_29_o1, memreg_30_o1, memreg_31_o1, memreg_32_o1, multiplexer_1_out;

  Decoder #(.select(5)) decoder_1 (
    .out0(decoder_1_out0), .out1(decoder_1_out1), .out2(decoder_1_out2), .out3(decoder_1_out3),
    .out4(decoder_1_out4), .out5(decoder_1_out5), .out6(decoder_1_out6), .out7(decoder_1_out7),
    .out8(decoder_1_out8), .out9(decoder_1_out9), .out10(decoder_1_out10), .out11(decoder_1_out11),
    .out12(decoder_1_out12), .out13(decoder_1_out13), .out14(decoder_1_out14), .out15(decoder_1_out15),
    .out16(decoder_1_out16), .out17(decoder_1_out17), .out18(decoder_1_out18), .out19(decoder_1_out19),
    .out20(decoder_1_out20), .out21(decoder_1_out21), .out22(decoder_1_out22), .out23(decoder_1_out23),
    .out24(decoder_1_out24), .out25(decoder_1_out25), .out26(decoder_1_out26), .out27(decoder_1_out27),
    .out28(decoder_1_out28), .out29(decoder_1_out29), .out30(decoder_1_out30), .out31(decoder_1_out31),
    .sel(Add_IN[4:0]), .en(WR));
  Demultiplexer #(.select(5), .width(16)) demultiplexer_1 (
    .out0(demultiplexer_1_out0), .out1(demultiplexer_1_out1), .out2(demultiplexer_1_out2),
    .out3(demultiplexer_1_out3), .out4(demultiplexer_1_out4), .out5(demultiplexer_1_out5),
    .out6(demultiplexer_1_out6), .out7(demultiplexer_1_out7), .out8(demultiplexer_1_out8),
    .out9(demultiplexer_1_out9), .out10(demultiplexer_1_out10), .out11(demultiplexer_1_out11),
    .out12(demultiplexer_1_out12), .out13(demultiplexer_1_out13), .out14(demultiplexer_1_out14),
    .out15(demultiplexer_1_out15), .out16(demultiplexer_1_out16), .out17(demultiplexer_1_out17),
    .out18(demultiplexer_1_out18), .out19(demultiplexer_1_out19), .out20(demultiplexer_1_out20),
    .out21(demultiplexer_1_out21), .out22(demultiplexer_1_out22), .out23(demultiplexer_1_out23),
    .out24(demultiplexer_1_out24), .out25(demultiplexer_1_out25), .out26(demultiplexer_1_out26),
    .out27(demultiplexer_1_out27), .out28(demultiplexer_1_out28), .out29(demultiplexer_1_out29),
    .out30(demultiplexer_1_out30), .out31(demultiplexer_1_out31), .in(DATA_IN), .sel(Add_IN[4:0]));
  memreg memreg_1 (.I1(demultiplexer_1_out0), .LD(decoder_1_out0), .CK(CK), .O1(memreg_1_o1));
  memreg memreg_2 (.I1(demultiplexer_1_out8), .LD(decoder_1_out8), .CK(CK), .O1(memreg_2_o1));
  memreg memreg_3 (.I1(demultiplexer_1_out16), .LD(decoder_1_out16), .CK(CK), .O1(memreg_3_o1));
  memreg memreg_4 (.I1(demultiplexer_1_out24), .LD(decoder_1_out24), .CK(CK), .O1(memreg_4_o1));
  memreg memreg_5 (.I1(demultiplexer_1_out1), .LD(decoder_1_out1), .CK(CK), .O1(memreg_5_o1));
  memreg memreg_6 (.I1(demultiplexer_1_out9), .LD(decoder_1_out9), .CK(CK), .O1(memreg_6_o1));
  memreg memreg_7 (.I1(demultiplexer_1_out17), .LD(decoder_1_out17), .CK(CK), .O1(memreg_7_o1));
  memreg memreg_8 (.I1(demultiplexer_1_out25), .LD(decoder_1_out25), .CK(CK), .O1(memreg_8_o1));
  memreg memreg_9 (.I1(demultiplexer_1_out2), .LD(decoder_1_out2), .CK(CK), .O1(memreg_9_o1));
  memreg memreg_10 (.I1(demultiplexer_1_out10), .LD(decoder_1_out10), .CK(CK), .O1(memreg_10_o1));
  memreg memreg_11 (.I1(demultiplexer_1_out18), .LD(decoder_1_out18), .CK(CK), .O1(memreg_11_o1));
  memreg memreg_12 (.I1(demultiplexer_1_out26), .LD(decoder_1_out26), .CK(CK), .O1(memreg_12_o1));
  memreg memreg_13 (.I1(demultiplexer_1_out3), .LD(decoder_1_out3), .CK(CK), .O1(memreg_13_o1));
  memreg memreg_14 (.I1(demultiplexer_1_out11), .LD(decoder_1_out11), .CK(CK), .O1(memreg_14_o1));
  memreg memreg_15 (.I1(demultiplexer_1_out19), .LD(decoder_1_out19), .CK(CK), .O1(memreg_15_o1));
  memreg memreg_16 (.I1(demultiplexer_1_out27), .LD(decoder_1_out27), .CK(CK), .O1(memreg_16_o1));
  memreg memreg_17 (.I1(demultiplexer_1_out4), .LD(decoder_1_out4), .CK(CK), .O1(memreg_17_o1));
  memreg memreg_18 (.I1(demultiplexer_1_out12), .LD(decoder_1_out12), .CK(CK), .O1(memreg_18_o1));
  memreg memreg_19 (.I1(demultiplexer_1_out20), .LD(decoder_1_out20), .CK(CK), .O1(memreg_19_o1));
  memreg memreg_20 (.I1(demultiplexer_1_out28), .LD(decoder_1_out28), .CK(CK), .O1(memreg_20_o1));
  memreg memreg_21 (.I1(demultiplexer_1_out5), .LD(decoder_1_out5), .CK(CK), .O1(memreg_21_o1));
  memreg memreg_22 (.I1(demultiplexer_1_out13), .LD(decoder_1_out13), .CK(CK), .O1(memreg_22_o1));
  memreg memreg_23 (.I1(demultiplexer_1_out21), .LD(decoder_1_out21), .CK(CK), .O1(memreg_23_o1));
  memreg memreg_24 (.I1(demultiplexer_1_out29), .LD(decoder_1_out29), .CK(CK), .O1(memreg_24_o1));
  memreg memreg_25 (.I1(demultiplexer_1_out6), .LD(decoder_1_out6), .CK(CK), .O1(memreg_25_o1));
  memreg memreg_26 (.I1(demultiplexer_1_out14), .LD(decoder_1_out14), .CK(CK), .O1(memreg_26_o1));
  memreg memreg_27 (.I1(demultiplexer_1_out22), .LD(decoder_1_out22), .CK(CK), .O1(memreg_27_o1));
  memreg memreg_28 (.I1(demultiplexer_1_out30), .LD(decoder_1_out30), .CK(CK), .O1(memreg_28_o1));
  memreg memreg_29 (.I1(demultiplexer_1_out7), .LD(decoder_1_out7), .CK(CK), .O1(memreg_29_o1));
  memreg memreg_30 (.I1(demultiplexer_1_out15), .LD(decoder_1_out15), .CK(CK), .O1(memreg_30_o1));
  memreg memreg_31 (.I1(demultiplexer_1_out23), .LD(decoder_1_out23), .CK(CK), .O1(memreg_31_o1));
  memreg memreg_32 (.I1(demultiplexer_1_out31), .LD(decoder_1_out31), .CK(CK), .O1(memreg_32_o1));
  Multiplexer #(.enable("true"), .select(5), .width(16)) multiplexer_1 (
    .in0(memreg_1_o1), .in1(memreg_5_o1), .in2(memreg_9_o1), .in3(memreg_13_o1), .in4(memreg_17_o1),
    .in5(memreg_21_o1), .in6(memreg_25_o1), .in7(memreg_29_o1), .in8(memreg_2_o1), .in9(memreg_6_o1),
    .in10(memreg_10_o1), .in11(memreg_14_o1), .in12(memreg_18_o1), .in13(memreg_22_o1), .in14(memreg_26_o1),
    .in15(memreg_30_o1), .in16(memreg_3_o1), .in17(memreg_7_o1), .in18(memreg_11_o1), .in19(memreg_15_o1),
    .in20(memreg_19_o1), .in21(memreg_23_o1), .in22(memreg_27_o1), .in23(memreg_31_o1), .in24(memreg_4_o1),
    .in25(memreg_8_o1), .in26(memreg_12_o1), .in27(memreg_16_o1), .in28(memreg_20_o1), .in29(memreg_24_o1),
    .in30(memreg_28_o1), .in31(memreg_32_o1), .out(multiplexer_1_out), .sel(Add_IN[4:0]), .en(RD));
  memreg memreg_33 (.I1(multiplexer_1_out), .LD(RD), .CK(CK), .O1(O));

  // Other names for the same wires on the sheet: bit5[4:0] = Add_IN[4:0]; I1[15:0] = DATA_IN
endmodule

module memreg (
  input  LD,
  input  CK,
  input  [15:0] I1,
  output [15:0] O1
);

  wire and_1_out;

  and and_1 (and_1_out, LD, CK);
  D_Flip_Flop d1 (.D(I1[0]), .clk(and_1_out), .Q(O1[0]));  // open: Qn, preset, reset
  D_Flip_Flop d2 (.D(I1[1]), .clk(and_1_out), .Q(O1[1]));  // open: Qn, preset, reset
  D_Flip_Flop d3 (.D(I1[2]), .clk(and_1_out), .Q(O1[2]));  // open: Qn, preset, reset
  D_Flip_Flop d4 (.D(I1[3]), .clk(and_1_out), .Q(O1[3]));  // open: Qn, preset, reset
  D_Flip_Flop d5 (.D(I1[4]), .clk(and_1_out), .Q(O1[4]));  // open: Qn, preset, reset
  D_Flip_Flop d6 (.D(I1[5]), .clk(and_1_out), .Q(O1[5]));  // open: Qn, preset, reset
  D_Flip_Flop d7 (.D(I1[6]), .clk(and_1_out), .Q(O1[6]));  // open: Qn, preset, reset
  D_Flip_Flop d8 (.D(I1[7]), .clk(and_1_out), .Q(O1[7]));  // open: Qn, preset, reset
  D_Flip_Flop d9 (.D(I1[8]), .clk(and_1_out), .Q(O1[8]));  // open: Qn, preset, reset
  D_Flip_Flop d10 (.D(I1[9]), .clk(and_1_out), .Q(O1[9]));  // open: Qn, preset, reset
  D_Flip_Flop d11 (.D(I1[10]), .clk(and_1_out), .Q(O1[10]));  // open: Qn, preset, reset
  D_Flip_Flop d12 (.D(I1[11]), .clk(and_1_out), .Q(O1[11]));  // open: Qn, preset, reset
  D_Flip_Flop d13 (.D(I1[12]), .clk(and_1_out), .Q(O1[12]));  // open: Qn, preset, reset
  D_Flip_Flop d14 (.D(I1[13]), .clk(and_1_out), .Q(O1[13]));  // open: Qn, preset, reset
  D_Flip_Flop d15 (.D(I1[14]), .clk(and_1_out), .Q(O1[14]));  // open: Qn, preset, reset
  D_Flip_Flop d16 (.D(I1[15]), .clk(and_1_out), .Q(O1[15]));  // open: Qn, preset, reset

  // Notes on the sheet:
  //   output
endmodule

module ALU1 (
  input  [3:0] Timer,
  input  [15:0] IR,
  input  [15:0] AC,
  input  [15:0] DR,
  input  [7:0] INPR,
  input  Ebit,
  output [15:0] ALU_OP,
  output ExtendedBit
);

  wire adder_1_cout, and_1_out, and_4_out, and_5_out, and_6_out, and_7_out, and_8_out, and_9_out, and_10_out,
       and_11_out, D7BN15T3, decoder_1_out3, decoder_1_out5, decoder_2_out0, decoder_2_out1, decoder_2_out2,
       decoder_2_out7, multiplexer_1_out, not_1_out, not_3_out, not_4_out, or_1_out;
  wire [2:0] ALU_selector;
  wire [15:0] adder_1_out, ALU_INPR_16, and_3_out, not_2_out, shifter_1_out, shifter_2_out;

  Decoder #(.enable("false"), .select(4)) decoder_1 (
    .out3(decoder_1_out3), .out5(decoder_1_out5), .sel(Timer));  // open: out0, out1, out2, out4, out6, out7, out8, out9, out10, out11, out12, out13, out14, out15
  not not_1 (not_1_out, IR[15]);
  Decoder #(.enable("false"), .select(3)) decoder_2 (
    .out0(decoder_2_out0), .out1(decoder_2_out1), .out2(decoder_2_out2), .out7(decoder_2_out7),
    .sel(IR[14:12]));  // open: out3, out4, out5, out6
  and and_1 (and_1_out, IR[15], decoder_2_out7, decoder_1_out3);
  and and_2 (D7BN15T3, decoder_2_out7, not_1_out, decoder_1_out3);
  Adder #(.width(16)) adder_1 (.a(AC), .b(DR), .out(adder_1_out), .cout(adder_1_cout));  // open: cin
  Shifter #(.shift("lr"), .width(16)) shifter_1 (.in(AC), .\dist (4'b0001), .out(shifter_1_out));
  Shifter #(.width(16)) shifter_2 (.in(AC), .\dist (4'b0001), .out(shifter_2_out));
  assign not_2_out = ~AC;  // NOT_Gate not_2, 16 bits wide
  assign and_3_out = AC & DR;  // AND_Gate and_3, 16 bits wide
  Multiplexer #(.select(3)) multiplexer_1 (
    .in0(Ebit), .in1(Ebit), .in2(adder_1_cout), .in3(Ebit), .in4(Ebit), .in5(Ebit), .in6(AC[15]),
    .in7(AC[0]), .out(multiplexer_1_out), .sel(ALU_selector));
  Multiplexer #(.select(3), .width(16)) multiplexer_2 (
    .in0(AC), .in1(and_3_out), .in2(adder_1_out), .in3(DR), .in4(ALU_INPR_16), .in5(not_2_out),
    .in6({Ebit, shifter_1_out[14:0]}), .in7({shifter_2_out[15:1], Ebit}), .out(ALU_OP), .sel(ALU_selector));
  not not_3 (not_3_out, Ebit);
  Multiplexer multiplexer_3 (.in0(multiplexer_1_out), .in1(not_3_out), .out(ExtendedBit), .sel(and_4_out));
  and and_4 (and_4_out, IR[8], D7BN15T3);
  and and_5 (and_5_out, decoder_2_out0, decoder_1_out5);
  and and_6 (and_6_out, decoder_2_out1, decoder_1_out5);
  and and_7 (and_7_out, decoder_2_out2, decoder_1_out5);
  and and_8 (and_8_out, and_1_out, IR[11]);
  and and_9 (and_9_out, D7BN15T3, IR[6]);
  and and_10 (and_10_out, D7BN15T3, IR[7]);
  and and_11 (and_11_out, D7BN15T3, IR[10]);
  or or_1 (or_1_out, and_5_out, and_6_out, and_7_out, and_8_out, and_9_out, and_10_out, and_11_out);
  not not_4 (not_4_out, or_1_out);
  Priority_Encoder priority_encoder_1 (
    .in0(not_4_out), .in1(and_5_out), .in2(and_6_out), .in3(and_7_out), .in4(and_8_out), .in5(and_9_out),
    .in6(and_10_out), .in7(and_11_out), .out(ALU_selector));  // open: en_in, gs, en_out

  // Other names for the same wires on the sheet: ALU_INPR[7:0] = INPR; ALU_AC[15:0] = AC; ALU_DR[15:0] = DR
endmodule

module OUTR1 (
  input  CLR,
  input  LD,
  input  CK,
  input  [15:0] I1,
  output [7:0] O
);

  and and_1 (I1[4], CLR, CK);
  and and_2 (I1[4], LD, CK);
  D_Flip_Flop d_ff_1 (.D(I1[0]), .clk(I1[4]), .Q(O[0]), .reset(I1[4]));  // open: Qn, preset
  D_Flip_Flop d_ff_2 (.D(I1[1]), .clk(I1[4]), .Q(O[1]), .reset(I1[4]));  // open: Qn, preset
  D_Flip_Flop d_ff_3 (.D(I1[2]), .clk(I1[4]), .Q(O[2]), .reset(I1[4]));  // open: Qn, preset
  D_Flip_Flop d_ff_4 (.D(I1[3]), .clk(I1[4]), .Q(O[3]), .reset(I1[4]));  // open: Qn, preset
  D_Flip_Flop d_ff_5 (.D(I1[4]), .clk(I1[4]), .Q(O[4]), .reset(I1[4]));  // open: Qn, preset
  D_Flip_Flop d_ff_6 (.D(I1[5]), .clk(I1[4]), .Q(O[5]), .reset(I1[4]));  // open: Qn, preset
  D_Flip_Flop d_ff_7 (.D(I1[6]), .clk(I1[4]), .Q(O[6]), .reset(I1[4]));  // open: Qn, preset
  D_Flip_Flop d_ff_8 (.D(I1[7]), .clk(I1[4]), .Q(O[7]), .reset(I1[4]));  // open: Qn, preset

  // Other names for the same wires on the sheet: LD1 = LD
endmodule

module INPR1 (
  input  [7:0] I1,
  output [7:0] O
);


  assign O = I1;
endmodule

module AR_CONTROLLER (
  input  [15:0] IR,
  input  [3:0] Timer,
  input  R,
  output AR_LD,
  output AR_INC,
  output AR_CLR
);

  wire and_1_out, and_2_out, decoder_1_out0, decoder_1_out2, decoder_1_out3, decoder_1_out4, decoder_2_out5,
       decoder_2_out7, not_1_out, not_2_out, or_1_out;

  Decoder #(.enable("false"), .select(4)) decoder_1 (
    .out0(decoder_1_out0), .out2(decoder_1_out2), .out3(decoder_1_out3), .out4(decoder_1_out4), .sel(Timer));  // open: out1, out5, out6, out7, out8, out9, out10, out11, out12, out13, out14, out15
  not not_1 (not_1_out, R);
  Decoder #(.enable("false"), .select(3)) decoder_2 (
    .out5(decoder_2_out5), .out7(decoder_2_out7), .sel(IR[14:12]));  // open: out0, out1, out2, out3, out4, out6
  not not_2 (not_2_out, decoder_2_out7);
  or or_1 (or_1_out, decoder_1_out0, decoder_1_out2);
  and and_1 (and_1_out, or_1_out, not_1_out);
  and and_2 (and_2_out, decoder_1_out3, IR[15], not_2_out);
  or or_2 (AR_LD, and_1_out, and_2_out);
  and and_3 (AR_INC, decoder_1_out4, decoder_2_out5);
  and and_4 (AR_CLR, decoder_1_out0, R);
endmodule

module DR_CONTROLLER (
  input  [15:0] IR,
  input  [3:0] Timer,
  output DR_LD,
  output DR_INC
);

  wire decoder_1_out4, decoder_1_out5, decoder_2_out0, decoder_2_out1, decoder_2_out2, decoder_2_out6,
       or_1_out;

  Decoder #(.enable("false"), .select(4)) decoder_1 (
    .out4(decoder_1_out4), .out5(decoder_1_out5), .sel(Timer));  // open: out0, out1, out2, out3, out6, out7, out8, out9, out10, out11, out12, out13, out14, out15
  Decoder #(.enable("false"), .select(3)) decoder_2 (
    .out0(decoder_2_out0), .out1(decoder_2_out1), .out2(decoder_2_out2), .out6(decoder_2_out6),
    .sel(IR[14:12]));  // open: out3, out4, out5, out7
  or or_1 (or_1_out, decoder_2_out0, decoder_2_out1, decoder_2_out2, decoder_2_out6);
  and and_1 (DR_LD, or_1_out, decoder_1_out4);
  and and_2 (DR_INC, decoder_2_out6, decoder_1_out5);
endmodule

module TR_CONTROLLER (
  input  R,
  input  [3:0] Timer,
  output TR_LD
);

  wire decoder_1_out0;

  Decoder #(.enable("false"), .select(4)) decoder_1 (
    .out0(decoder_1_out0), .sel(Timer));  // open: out1, out2, out3, out4, out5, out6, out7, out8, out9, out10, out11, out12, out13, out14, out15
  and and_1 (TR_LD, decoder_1_out0, R);
endmodule

module OUTR_CONTROLLER (
  input  [15:0] IR,
  input  [3:0] Timer,
  output OUTR_LD
);

  wire and_1_out, decoder_1_out3, decoder_2_out7;

  Decoder #(.enable("false"), .select(4)) decoder_1 (
    .out3(decoder_1_out3), .sel(Timer));  // open: out0, out1, out2, out4, out5, out6, out7, out8, out9, out10, out11, out12, out13, out14, out15
  Decoder #(.enable("false"), .select(3)) decoder_2 (
    .out7(decoder_2_out7), .sel(IR[14:12]));  // open: out0, out1, out2, out3, out4, out5, out6
  and and_1 (and_1_out, decoder_2_out7, decoder_1_out3, IR[15]);
  and and_2 (OUTR_LD, IR[10], and_1_out);
endmodule

module IR_CONTROLLER (
  input  R,
  input  [3:0] Timer,
  output IR_LD
);

  wire decoder_1_out1, not_1_out;

  Decoder #(.enable("false"), .select(4)) decoder_1 (
    .out1(decoder_1_out1), .sel(Timer));  // open: out0, out2, out3, out4, out5, out6, out7, out8, out9, out10, out11, out12, out13, out14, out15
  not not_1 (not_1_out, R);
  and and_1 (IR_LD, decoder_1_out1, not_1_out);
endmodule

module PC_CONTROLLER (
  input  [15:0] IR,
  input  [3:0] Timer,
  input  R,
  input  [15:0] DR,
  input  [15:0] AC,
  input  E,
  input  FGI,
  input  FGO,
  output PC_LD,
  output PC_INC,
  output PC_CLR
);

  wire AC15, AC15_not, AC_t, and_1_out, and_2_out, and_3_out, and_4_out, and_5_out, and_6_out, and_7_out,
       and_8_out, and_9_out, and_10_out, and_11_out, and_12_out, and_13_out, and_14_out, and_15_out, D6, D7,
       decoder_1_out5, decoder_2_out4, decoder_2_out5, DR_t, not_3_out, or_1_out, or_2_out, R_not, T1, T2,
       T4, T6;

  Comparator #(.width(16)) comparator_1 (.a(DR), .b({16{1'b0}}), .eq(DR_t));  // open: gt, lt
  Comparator #(.width(16)) comparator_2 (.a(AC), .b({16{1'b0}}), .eq(AC_t));  // open: gt, lt
  Comparator #(.width(1)) comparator_3 (.a(AC[15]), .b(1'b0), .eq(AC15));  // open: gt, lt
  Decoder #(.enable("false"), .select(4)) decoder_1 (
    .out1(T1), .out2(T2), .out4(T4), .out5(decoder_1_out5), .out6(T6), .sel(Timer));  // open: out0, out3, out7, out8, out9, out10, out11, out12, out13, out14, out15
  not not_1 (R_not, R);
  not not_2 (AC15_not, AC15);
  Decoder #(.enable("false"), .select(3)) decoder_2 (
    .out4(decoder_2_out4), .out5(decoder_2_out5), .out6(D6), .out7(D7), .sel(IR[14:12]));  // open: out0, out1, out2, out3
  and and_1 (and_1_out, AC15_not, IR[4]);
  and and_2 (and_2_out, IR[3], AC15);
  and and_3 (and_3_out, IR[2], AC_t);
  and and_4 (and_4_out, IR[1], E);
  and and_5 (and_5_out, FGI, IR[9]);
  and and_6 (and_6_out, FGO, IR[8]);
  and and_7 (and_7_out, decoder_2_out4, T4);
  and and_8 (and_8_out, decoder_2_out5, decoder_1_out5);
  not not_3 (not_3_out, IR[15]);
  and and_9 (and_9_out, D7, not_3_out, T4);
  or or_1 (or_1_out, and_1_out, and_2_out, and_3_out, and_4_out);
  and and_10 (and_10_out, D7, IR[15], T4);
  or or_2 (or_2_out, and_5_out, and_6_out);
  or or_3 (PC_LD, and_7_out, and_8_out);
  and and_11 (and_11_out, T1, R_not);
  and and_12 (and_12_out, T2, R);
  and and_13 (and_13_out, D6, T6, DR_t);
  and and_14 (and_14_out, and_9_out, or_1_out);
  and and_15 (and_15_out, and_10_out, or_2_out);
  or or_4 (PC_INC, and_11_out, and_12_out, and_13_out, and_14_out, and_15_out);
  and and_16 (PC_CLR, T1, R);

  // Other names for the same wires on the sheet: B1 = IR[1]; B2 = IR[2]; B3 = IR[3]; B4 = IR[4]; B8 = IR[8];
  //   B9 = IR[9]; B15 = IR[15]
endmodule

module SCOUNTER (
  input  CLR,
  input  LD,
  input  STRT,
  input  [3:0] I,
  input  CLK,
  output [3:0] O,
  output Cry
);

  wire and_1_out, and_2_out, and_3_out, and_4_out, and_5_out, and_6_out, and_7_out, and_8_out, and_9_out,
       and_10_out, and_11_out, and_12_out, and_13_out, not_1_out, not_2_out, not_3_out, not_4_out, not_5_out,
       not_6_out, or_1_out, or_2_out, or_3_out, or_4_out, or_5_out, or_6_out, or_7_out, or_8_out;

  not not_1 (not_1_out, CLR);
  not not_2 (not_2_out, LD);
  not not_3 (not_3_out, I[0]);
  not not_4 (not_4_out, I[1]);
  not not_5 (not_5_out, I[2]);
  not not_6 (not_6_out, I[3]);
  and and_1 (and_1_out, not_1_out, LD);
  and and_2 (and_2_out, not_1_out, not_2_out, STRT);
  and and_3 (and_3_out, and_1_out, I[0]);
  and and_4 (and_4_out, not_3_out, and_1_out);
  and and_5 (and_5_out, and_1_out, I[1]);
  and and_6 (and_6_out, not_4_out, and_1_out);
  and and_7 (and_7_out, and_1_out, I[2]);
  and and_8 (and_8_out, not_5_out, and_1_out);
  and and_9 (and_9_out, and_1_out, I[3]);
  and and_10 (and_10_out, not_6_out, and_1_out);
  and and_11 (and_11_out, and_2_out, O[0]);
  and and_12 (and_12_out, and_11_out, O[1]);
  and and_13 (and_13_out, and_12_out, O[2]);
  and and_14 (Cry, and_13_out, O[3]);
  or or_1 (or_1_out, and_2_out, and_3_out);
  or or_2 (or_2_out, CLR, and_2_out, and_4_out);
  or or_3 (or_3_out, and_11_out, and_5_out);
  or or_4 (or_4_out, CLR, and_11_out, and_6_out);
  or or_5 (or_5_out, and_12_out, and_7_out);
  or or_6 (or_6_out, CLR, and_12_out, and_8_out);
  or or_7 (or_7_out, and_13_out, and_9_out);
  or or_8 (or_8_out, CLR, and_13_out, and_10_out);
  J_K_Flip_Flop j_k_ff_1 (.J(or_1_out), .K(or_2_out), .clk(CLK), .Q(O[0]));  // open: Qn, preset, reset
  J_K_Flip_Flop j_k_ff_2 (.J(or_3_out), .K(or_4_out), .clk(CLK), .Q(O[1]));  // open: Qn, preset, reset
  J_K_Flip_Flop j_k_ff_3 (.J(or_5_out), .K(or_6_out), .clk(CLK), .Q(O[2]));  // open: Qn, preset, reset
  J_K_Flip_Flop j_k_ff_4 (.J(or_7_out), .K(or_8_out), .clk(CLK), .Q(O[3]));  // open: Qn, preset, reset
endmodule

module AC_CONTROLLER (
  input  [15:0] IR,
  input  [3:0] Timer,
  output AC_INC,
  output AC_CLR,
  output AC_LD
);

  wire and_1_out, and_2_out, and_5_out, and_6_out, and_7_out, decoder_1_out3, decoder_1_out5, decoder_2_out0,
       decoder_2_out1, decoder_2_out2, decoder_2_out7, not_1_out, or_1_out, or_2_out;

  Decoder #(.enable("false"), .select(4)) decoder_1 (
    .out3(decoder_1_out3), .out5(decoder_1_out5), .sel(Timer));  // open: out0, out1, out2, out4, out6, out7, out8, out9, out10, out11, out12, out13, out14, out15
  or or_1 (or_1_out, IR[9], IR[6], IR[7]);
  not not_1 (not_1_out, IR[15]);
  Decoder #(.enable("false"), .select(3)) decoder_2 (
    .out0(decoder_2_out0), .out1(decoder_2_out1), .out2(decoder_2_out2), .out7(decoder_2_out7),
    .sel(IR[14:12]));  // open: out3, out4, out5, out6
  or or_2 (or_2_out, decoder_2_out0, decoder_2_out1, decoder_2_out2);
  and and_1 (and_1_out, decoder_2_out7, not_1_out, decoder_1_out3);
  and and_2 (and_2_out, decoder_2_out7, IR[15], decoder_1_out3);
  and and_3 (AC_INC, IR[5], and_1_out);
  and and_4 (AC_CLR, and_1_out, IR[11]);
  and and_5 (and_5_out, or_2_out, decoder_1_out5);
  and and_6 (and_6_out, and_1_out, or_1_out);
  and and_7 (and_7_out, IR[11], and_2_out);
  or or_3 (AC_LD, and_5_out, and_6_out, and_7_out);
endmodule

module BUS_Encoder_8x3 (
  input  X1,
  input  X2,
  input  X3,
  input  X4,
  input  X5,
  input  X6,
  input  X7,
  output S0,
  output S1,
  output S2
);

  or or_1 (S0, X1, X3, X5, X7);
  or or_2 (S1, X2, X3, X6, X7);
  or or_3 (S2, X4, X5, X6, X7);
endmodule

module BUS_CONTROLLE1R (
  input  [15:0] IR,
  input  [3:0] Timer,
  input  R,
  output X1,
  output X2,
  output X3,
  output X4,
  output X5,
  output X6,
  output X7
);

  wire and_1_out, and_2_out, and_3_out, and_4_out, and_5_out, and_6_out, and_7_out, and_8_out, and_9_out, D0,
       D1, D2, D3, D4, D5, D6, D7, decoder_2_out7, or_1_out, or_2_out, R_not, t0, t1, t2, t3, t4, t5, t6;

  Decoder #(.enable("false"), .select(4)) decoder_1 (
    .out0(t0), .out1(t1), .out2(t2), .out3(t3), .out4(t4), .out5(t5), .out6(t6), .sel(Timer));  // open: out7, out8, out9, out10, out11, out12, out13, out14, out15
  not not_1 (R_not, R);
  Decoder #(.enable("false"), .select(3)) decoder_2 (
    .out0(D0), .out1(D1), .out2(D2), .out3(D3), .out4(D4), .out5(D5), .out6(D6), .out7(decoder_2_out7),
    .sel(IR[14:12]));
  not not_2 (D7, decoder_2_out7);
  or or_1 (or_1_out, D0, D1, D2, D6);
  or or_2 (or_2_out, R_not, R);
  and and_1 (and_1_out, D4, t4);
  and and_2 (and_2_out, D5, t5);
  and and_3 (and_3_out, D5, t4);
  and and_4 (and_4_out, or_2_out, t0);
  and and_5 (and_5_out, D2, t5);
  and and_6 (and_6_out, D6, t6);
  and and_7 (and_7_out, R_not, t1);
  and and_8 (and_8_out, D7, IR[15], t3);
  and and_9 (and_9_out, t4, or_1_out);
  or or_3 (X1, and_1_out, and_2_out);
  or or_4 (X2, and_3_out, and_4_out);
  or or_5 (X3, and_5_out, and_6_out);
  and and_10 (X4, D3, t4);
  and and_11 (X5, R_not, t2);
  and and_12 (X6, R, t1);
  or or_6 (X7, and_7_out, and_8_out, and_9_out);

  // Other names for the same wires on the sheet: B15 = IR[15]
endmodule

module RAM_CU (
  input  [15:0] IR,
  input  [3:0] Timer,
  input  R,
  output Read,
  output Write
);

  wire and_1_out, and_2_out, and_3_out, and_4_out, and_5_out, and_6_out, and_7_out, D0, D1, D2, D3, D4, D5,
       D6, D7_not, decoder_2_out7, or_1_out, R_not, t0, t1, t2, t3, t4, t5, t6;

  Decoder #(.enable("false"), .select(4)) decoder_1 (
    .out0(t0), .out1(t1), .out2(t2), .out3(t3), .out4(t4), .out5(t5), .out6(t6), .sel(Timer));  // open: out7, out8, out9, out10, out11, out12, out13, out14, out15
  not not_1 (R_not, R);
  Decoder #(.enable("false"), .select(3)) decoder_2 (
    .out0(D0), .out1(D1), .out2(D2), .out3(D3), .out4(D4), .out5(D5), .out6(D6), .out7(decoder_2_out7),
    .sel(IR[14:12]));
  not not_2 (D7_not, decoder_2_out7);
  or or_1 (or_1_out, D0, D1, D2, D6);
  and and_1 (and_1_out, or_1_out, t4);
  and and_2 (and_2_out, D7_not, IR[15], t3);
  and and_3 (and_3_out, t1, R_not);
  and and_4 (and_4_out, R, t1);
  and and_5 (and_5_out, D3, t4);
  and and_6 (and_6_out, D5, t4);
  and and_7 (and_7_out, D6, t6);
  or or_2 (Read, and_1_out, and_2_out, and_3_out);
  or or_3 (Write, and_4_out, and_5_out, and_6_out, and_7_out);

  // Other names for the same wires on the sheet: B15 = IR[15]
endmodule

module SC_CONTROLLER (
  input  [15:0] IR,
  input  [3:0] Timer,
  input  R,
  output SC_CLR_Out
);

  wire and_1_out, and_2_out, and_3_out, and_4_out, and_5_out, and_6_out, and_7_out, and_8_out, and_9_out,
       and_10_out, D0, D1, D2, D3, D4, D5, D6, D7, not_2_out, R_not, t0, t1, t2, t3, t4, t5, t6;

  Decoder #(.enable("false"), .select(4)) decoder_1 (
    .out0(t0), .out1(t1), .out2(t2), .out3(t3), .out4(t4), .out5(t5), .out6(t6), .sel(Timer));  // open: out7, out8, out9, out10, out11, out12, out13, out14, out15
  not not_1 (R_not, R);
  Decoder #(.enable("false"), .select(3)) decoder_2 (
    .out0(D0), .out1(D1), .out2(D2), .out3(D3), .out4(D4), .out5(D5), .out6(D6), .out7(D7), .sel(IR[14:12]));
  not not_2 (not_2_out, IR[15]);
  and and_1 (and_1_out, D7, not_2_out, t3);
  and and_2 (and_2_out, D7, IR[15], t3);
  and and_3 (and_3_out, D6, t6);
  and and_4 (and_4_out, D5, t5);
  and and_5 (and_5_out, D4, t4);
  and and_6 (and_6_out, D3, t4);
  and and_7 (and_7_out, D2, t5);
  and and_8 (and_8_out, D1, t5);
  and and_9 (and_9_out, D0, t5);
  and and_10 (and_10_out, t2, R);
  or or_1 (SC_CLR_Out, and_1_out, and_2_out, and_3_out, and_4_out, and_5_out, and_6_out, and_7_out, and_8_out, and_9_out, and_10_out);

  // Other names for the same wires on the sheet: B15 = IR[15]
endmodule

module FF_Controller1 (
  input  MCLK,
  input  STRT,
  input  [15:0] IR,
  input  [3:0] Timer,
  input  R,
  input  IEN,
  input  FGI,
  input  FGO,
  input  E_ALU_OUT,
  output MCK,
  output I_set,
  output S_set,
  output S_clr,
  output R_set,
  output R_clr,
  output IEN_set,
  output IEN_clr,
  output FGI_clr,
  output FGO_clr,
  output E_set,
  output E_clr
);

  wire and_2_out, and_3_out, and_4_out, and_5_out, and_6_out, and_7_out, and_8_out, and_9_out, B15_not, D7,
       FGIO, not_3_out, not_4_out, not_5_out, R_not, t0, t1, t2, t3, t4, t5, t6;

  Decoder #(.enable("false"), .select(4)) decoder_1 (
    .out0(t0), .out1(t1), .out2(t2), .out3(t3), .out4(t4), .out5(t5), .out6(t6), .sel(Timer));  // open: out7, out8, out9, out10, out11, out12, out13, out14, out15
  not not_1 (R_not, R);
  and and_1 (FGIO, FGI, FGO);
  not not_2 (B15_not, IR[15]);
  Decoder #(.enable("false"), .select(3)) decoder_2 (
    .out7(D7), .sel(IR[14:12]));  // open: out0, out1, out2, out3, out4, out5, out6
  and and_2 (and_2_out, D7, IR[15], t3);
  and and_3 (and_3_out, D7, B15_not, t3);
  and and_4 (and_4_out, D7, B15_not, t3);
  not not_3 (not_3_out, t0);
  not not_4 (not_4_out, t1);
  not not_5 (not_5_out, t2);
  and and_5 (and_5_out, D7, IR[15], t3);
  and and_6 (and_6_out, IR[6], and_2_out);
  and and_7 (and_7_out, R, t2);
  and and_8 (and_8_out, D7, IR[15], t3);
  and and_9 (and_9_out, D7, IR[15], t3);
  and and_10 (I_set, R_not, t2);
  and and_11 (S_clr, and_4_out, IR[0]);
  and and_12 (R_set, not_3_out, not_4_out, not_5_out, IEN, FGIO);
  and and_13 (R_clr, R, t2);
  and and_14 (IEN_set, and_5_out, IR[7]);
  and and_15 (IEN_clr, and_6_out, and_7_out);
  and and_16 (FGI_clr, and_8_out, IR[11]);
  and and_17 (FGO_clr, and_9_out, IR[10]);
  and and_18 (E_clr, and_3_out, IR[10]);

  assign E_set = E_ALU_OUT;
  assign MCK = MCLK;
  assign S_set = STRT;

  // Other names for the same wires on the sheet: B0 = IR[0]; B6 = IR[6]; B7 = IR[7]; B10 = IR[10]; B11 = IR[11];
  //   B15 = IR[15]
endmodule

module BUS_BLOCK1 (
  input  [15:0] AR,
  input  [15:0] PC,
  input  [15:0] DR,
  input  [15:0] AC,
  input  [15:0] IR,
  input  [15:0] TR,
  input  [15:0] MEM,
  input  S0,
  input  S1,
  input  S2,
  output [15:0] O
);

  Multiplexer #(.select(3), .width(16)) multiplexer_1 (
    .in1(AR), .in2(PC), .in3(DR), .in4(AC), .in5(IR), .in6(TR), .in7(MEM), .out(O), .sel({S2, S1, S0}));  // open: in0
endmodule
